# Fritzing sketch SensorDistanciaCovid19_v1.X.X (saved by Fritzing 0.9.3b)

parts:
  Arduino = Arduino Nano (Rev3.0) (ICSP)
  SP1 = SPEAKER [package=pcb_mount_speaker]
  hc-sr1 = hc-sr04

nets:
  N1: Arduino.D3, SP1.+
  N2: Arduino.D5, hc-sr1.Echo
  N3: Arduino.D6, hc-sr1.Trig
  GND: Arduino.GND, SP1.-, hc-sr1.GND
  5V: Arduino.5V, hc-sr1.VCC

custom parts:
  hc-sr04: This is a HC-SR04 Distance Sensor (based on HC-SR04 Fritzing Project)
